# Fritzing sketch micro (saved by Fritzing 0.9.4)
breadboards: 1

parts:
  Part1 = Arduino Uno (Rev3)
  J1 = Piezo Speaker
  J2 = Piezo Speaker
  R1 = Resistor [tolerance=±5% resistance=1k package=THT]
  R2 = Resistor [tolerance=±5% resistance=1k package=THT]
  MX_switch = SWITCH-MOMENTARY-2 [package=tactile-switch-1101ne]
  R3 = Resistor [tolerance=±5% resistance=10k package=THT]
  Part2 = ws2812b [package="smd 2812b"]
  VCC1 = 4 x AAA Battery Mount
  R4 = Resistor [tolerance=±5% resistance=330 package=THT]

nets:
  N1: Part1.D8, J2.pin2
  N2: Part1.D9_PWM, J1.pin2
  GND: Part1.GND, R1.Pin_0, R2.Pin_0, R3.Pin_0, Part2.VSS, VCC1.-
  N3: Part1.D2, MX_switch.2, R3.Pin_1
  N4: Part1.D7, R4.Pin_0
  5V: Part1.5V, MX_switch.1, Part2.VDD, VCC1.+
  N5: J1.pin1, R2.Pin_1
  N6: J2.pin1, R1.Pin_1
  N7: Part2.DIN, R4.Pin_1
